# Fritzing sketch JediSlider (saved by Fritzing 0.9.3b)
breadboards: 1

parts:
  HC-SR04_Sensor_1 = HC-SR04 Ultrasonic Distance Sensor
  Componente1 = Arduino Leonardo (Rev3b)

nets:
  VCC: HC-SR04_Sensor_1.VCC, Componente1.5V
  N1: HC-SR04_Sensor_1.TRIG, Componente1.D12/A11
  N2: HC-SR04_Sensor_1.ECHO, Componente1.D13_PWM
  GND: HC-SR04_Sensor_1.GND, Componente1.D2/SDA, Componente1.GND, Componente1.SDA
